# Fritzing sketch Hello World - Liquid Crystal (saved by Fritzing 0.9.3b)
breadboards: 1

parts:
  Componente1 = Arduino Uno (Rev3)
  LCD1 = LCD screen
  R1 = Resistor [tolerance=±5% resistance=300 package=THT]
  R2 = Trimmer Potentiometer [maximum_resistance=10kΩ package=THT]

nets:
  N1: Componente1.D11_PWM/MOSI, LCD1.E
  N2: Componente1.D12/MISO, LCD1.RS
  N3: Componente1.D2, LCD1.DB7
  N4: Componente1.D3_PWM, LCD1.DB6
  N5: Componente1.D4, LCD1.DB5
  N6: Componente1.D5_PWM, LCD1.DB4
  5V: Componente1.5V, LCD1.VDD, R1.Pin_1, R2.leg1
  GND: Componente1.GND, LCD1.VSS, LCD1.R/W, LCD1.LED-, R2.leg2
  N7: LCD1.V0, R2.wiper
  N8: LCD1.LED+, R1.Pin_0

// code stored in the sketch: Hello World - Liquid Crystal.ino

// include the library code:

#include <LiquidCrystal.h>


// initialize the library by associating any needed LCD interface pin

// with the arduino pin number it is connected to

const int rs = 12, en = 11, d4 = 5, d5 = 4, d6 = 3, d7 = 2;

LiquidCrystal lcd(rs, en, d4, d5, d6, d7);


void setup() {

  // set up the LCD's number of columns and rows:

  lcd.begin(16, 2);

}


void loop() {
   for (int i = 0; i <= 32; i++) {
     lcd.setCursor(i-13, 0);
     lcd.print("h");
     lcd.setCursor(i-12, 0);
     lcd.print("e");
     lcd.setCursor(i-11, 0);
     lcd.print("l");
     lcd.setCursor(i-10, 0);
     lcd.print("l");
     lcd.setCursor(i-9, 0);
     lcd.print("o");
     lcd.setCursor(i-8, 0);
     lcd.print(",");
     lcd.setCursor(i-7, 0);
     lcd.print(" ");
     lcd.setCursor(i-6, 0);
     lcd.print("w");
     lcd.setCursor(i-5, 0);
     lcd.print("o");
     lcd.setCursor(i-4, 0);
     lcd.print("r");
     lcd.setCursor(i-3, 0);
     lcd.print("l");
     lcd.setCursor(i-2, 0);
     lcd.print("d");
     lcd.setCursor(i-1, 0);
     lcd.print("!");
     delay(800);
     lcd.clear();
   }

}
